// Logisim project ac_2122v_tp2.circ as structural Verilog: 6 circuits, main circuit CPU
module CPU (
);

  wire alu_1_z, CP1, CP2, d_ff_1_p4, EF, ER, Flags, MCLK_out, not_2_out, nRD, nWR, RST, SC, SI, SO;
  wire [1:0] interconnections_1_aa, interconnections_1_ab, interconnections_1_ad, OPA, SD, SE;
  wire [2:0] Opcode;
  wire [5:0] interconnections_1_imm;
  wire [7:0] adder_1_out, alu_1_r, controlled_buffer_1_out, Ext_output, multiplexer_1_out, multiplexer_2_out,
       multiplexer_3_out, multiplexer_4_out, PC_q, Register_File_a, Register_File_b, Register_File_c,
       Register_File_r0, Register_File_r1, Register_File_r2, Register_File_r3;
  wire [8:0] Code_memory_data;

  Instruction_Decoder instruction_decoder_1 (
    .Opcode(Opcode), .Flags(Flags), .nRD(nRD), .nWR(nWR), .EF(EF), .SC(SC), .SE(SE), .ER(ER), .OPA(OPA),
    .SI(SI), .SO(SO), .SD(SD));
  Multiplexer #(.width(8), .disabled(0), .enable("false")) multiplexer_1 (
    .in0(8'h1), .in1(Ext_output), .out(multiplexer_1_out), .sel(SO));
  Clock MCLK (.out(MCLK_out));
  Button MRST (.out(RST));
  Adder adder_1 (.a(PC_q), .b(multiplexer_1_out), .out(adder_1_out));  // open: cin, cout
  Multiplexer #(.width(8), .disabled(0), .enable("false")) multiplexer_2 (
    .in0(adder_1_out), .in1(Register_File_b), .out(multiplexer_2_out), .sel(SI));
  Register PC (.D(multiplexer_2_out), .Q(PC_q), .clk(CP1), .clr(RST));  // open: en
  or or_1 (CP1, MCLK_out, d_ff_1_p4);
  // D_Flip_Flop #(.NegatePresetClear("false")) d_ff_1: pin names not known; wires that end beside it: 1'b1, MCLK_out, RST, d_ff_1_p4
  not not_1 (CP2, CP1);
  ROM #(.dataWidth(9)) Code_memory (.addr(PC_q), .data(Code_memory_data));  // open: sel
  Interconnections interconnections_1 (
    .Instruction(Code_memory_data), .AB(interconnections_1_ab), .AA(interconnections_1_aa),
    .AD(interconnections_1_ad), .Opcode(Opcode), .Imm(interconnections_1_imm));
  // Probe on Code_memory_data
  Register_File Register_File (
    .AD(interconnections_1_ad), .WE(ER), .Clk(CP1), .D(multiplexer_4_out), .A(Register_File_a),
    .B(Register_File_b), .R0(Register_File_r0), .R1(Register_File_r1), .R2(Register_File_r2),
    .R3(Register_File_r3), .C(Register_File_c), .AA(interconnections_1_aa), .AB(interconnections_1_ab));
  // Probe on Register_File_r0
  // Probe on Register_File_r1
  // Probe on Register_File_r2
  // Probe on Register_File_r3
  Ext Ext (.Input(interconnections_1_imm), .Output(Ext_output), .Sel(SE));
  // Probe on Ext_output
  // Probe on Register_File_c
  // Probe on Register_File_a
  // Probe on Register_File_b
  Multiplexer #(.width(8), .enable("false")) multiplexer_3 (
    .in0(Register_File_b), .in1(Ext_output), .out(multiplexer_3_out), .sel(SC));
  ALU alu_1 (.A(Register_File_a), .B(multiplexer_3_out), .Z(alu_1_z), .R(alu_1_r), .OP(OPA));
  not not_2 (not_2_out, nWR);
  // Probe on alu_1_r
  Register #(.width(1)) CPSR (.D(alu_1_z), .en(EF), .Q(Flags), .clk(CP1));  // open: clr
  assign controlled_buffer_1_out = not_2_out ? Register_File_c : 8'bz;  // Controlled_Buffer controlled_buffer_1
  // Probe on controlled_buffer_1_out
  RAM #(.bus("synch")) Data_memory (.addr(alu_1_r), .data(controlled_buffer_1_out));  // open: sel, clk, ld, clr
  Multiplexer #(.select(2), .width(8), .enable("false")) multiplexer_4 (
    .in0(controlled_buffer_1_out), .in1(alu_1_r), .in2(Ext_output), .out(multiplexer_4_out), .sel(SD));  // open: in3
  // Probe on multiplexer_4_out

  // Notes on the sheet:
  //   contents of Code_memory (hex, n*v repeats v):
  //   80 10 1b0 c7 45 121 195 1aa 196 b8 1c ac 1c2
endmodule

module Register_File (
  input  Clk,
  input  [7:0] D,
  input  WE,
  input  [1:0] AD,
  input  [1:0] AB,
  input  [1:0] AA,
  output [7:0] R3,
  output [7:0] R2,
  output [7:0] R1,
  output [7:0] R0,
  output [7:0] A,
  output [7:0] B,
  output [7:0] C
);

  wire demultiplexer_1_out0, demultiplexer_1_out1, demultiplexer_1_out2, demultiplexer_1_out3;

  Demultiplexer #(.select(2), .disabled(0), .enable("false")) demultiplexer_1 (
    .out0(demultiplexer_1_out0), .out1(demultiplexer_1_out1), .out2(demultiplexer_1_out2),
    .out3(demultiplexer_1_out3), .in(WE), .sel(AD));
  Register u_R0 (.D(D), .en(demultiplexer_1_out0), .Q(R0), .clk(Clk));  // open: clr
  Register u_R1 (.D(D), .en(demultiplexer_1_out1), .Q(R1), .clk(Clk));  // open: clr
  Register u_R2 (.D(D), .en(demultiplexer_1_out2), .Q(R2), .clk(Clk));  // open: clr
  Register u_R3 (.D(D), .en(demultiplexer_1_out3), .Q(R3), .clk(Clk));  // open: clr
  Multiplexer #(.select(2), .width(8), .disabled(0), .enable("false")) multiplexer_1 (
    .in0(R0), .in1(R1), .in2(R2), .in3(R3), .out(C), .sel(AD));
  Multiplexer #(.select(2), .width(8), .disabled(0), .enable("false")) multiplexer_2 (
    .in0(R0), .in1(R1), .in2(R2), .in3(R3), .out(B), .sel(AB));
  Multiplexer #(.select(2), .width(8), .disabled(0), .enable("false")) multiplexer_3 (
    .in0(R0), .in1(R1), .in2(R2), .in3(R3), .out(A), .sel(AA));
endmodule

module Instruction_Decoder (
  input  Flags,
  input  [2:0] Opcode,
  output [1:0] SD,
  output nRD,
  output nWR,
  output EF,
  output SC,
  output [1:0] SE,
  output ER,
  output SI,
  output SO,
  output [1:0] OPA
);

  ROM #(.addrWidth(4), .dataWidth(11)) rom_1 (
    .addr({Opcode, Flags}), .data({SD, nRD, nWR, EF, SC, SE, ER, SI, SO}));  // open: sel

  assign OPA = Opcode[1:0];

  // Notes on the sheet:
  //   contents of rom_1 (hex, n*v repeats v):
  //   84 84 1e0 1e1 5b0 5b0 f0 f0 ac ac 3f8 3f8 3c4 3c4 c2 c2
endmodule

module ALU (
  input  [7:0] A,
  input  [7:0] B,
  input  [1:0] OP,
  output [7:0] R,
  output Z
);

  wire [7:0] adder_1_out, bit_extender_1_out, bit_extender_2_out, nor_1_out, xor_1_out, xor_2_out;

  assign bit_extender_1_out = {{7{OP[0]}}, OP[0]};  // Bit_Extender bit_extender_1
  assign bit_extender_2_out = {{7{OP[0]}}, OP[0]};  // Bit_Extender bit_extender_2
  assign xor_1_out = A ^ bit_extender_1_out;  // XOR_Gate xor_1, 8 bits wide
  assign xor_2_out = B ^ bit_extender_2_out;  // XOR_Gate xor_2, 8 bits wide
  Adder adder_1 (.a(A), .b(xor_2_out), .out(adder_1_out), .cin(OP[0]));  // open: cout
  assign nor_1_out = ~(xor_1_out | xor_2_out);  // NOR_Gate nor_1, 8 bits wide
  Multiplexer #(.width(8), .enable("false")) multiplexer_1 (.in0(adder_1_out), .in1(nor_1_out), .out(R), .sel(OP[1]));
  nor nor_2 (Z, R[0], R[1], R[2], R[3], R[4], R[5], R[6], R[7]);
endmodule

module Interconnections (
  input  [8:0] Instruction,
  output [1:0] AB,
  output [1:0] AA,
  output [1:0] AD,
  output [5:0] Imm,
  output [2:0] Opcode
);


  assign AA = Instruction[3:2];
  assign AB = Instruction[1:0];
  assign AD = Instruction[5:4];
  assign Imm = Instruction[5:0];
  assign Opcode = Instruction[8:6];

  // Notes on the sheet:
  //   rm
  //   rn
  //   rd
endmodule

module Ext (
  input  [5:0] Input,
  input  [1:0] Sel,
  output [7:0] Output
);

  wire [7:0] bit_extender_1_out, bit_extender_2_out, bit_extender_3_out, bit_extender_4_out;

  assign bit_extender_1_out = {{2{Input[5]}}, Input};  // Bit_Extender bit_extender_1
  assign bit_extender_2_out = {{6{1'b0}}, Input[1:0]};  // Bit_Extender bit_extender_2
  assign bit_extender_3_out = {{4{1'b0}}, Input[3:0]};  // Bit_Extender bit_extender_3
  assign bit_extender_4_out = {{6{Input[1]}}, Input[1:0]};  // Bit_Extender bit_extender_4
  Multiplexer #(.select(2), .width(8), .enable("false")) multiplexer_1 (
    .in0(bit_extender_1_out), .in1(bit_extender_2_out), .in2(bit_extender_3_out), .in3(bit_extender_4_out),
    .out(Output), .sel(Sel));

  // Notes on the sheet:
  //   bzs
  //   ldr
  //   mov
  //   sub
endmodule
