// Logisim project ac_2223i_tp2_final.circ as structural Verilog: 9 circuits, main circuit CPU
module ALU (
  input  [7:0] A,
  input  [7:0] B,
  input  [1:0] OP,
  output [7:0] R,
  output Z
);

  wire [7:0] adder_1_out, barrel_shifter_1_y, bit_extender_1_out, multiplexer_1_out, xor_1_out;

  assign bit_extender_1_out = {{7{OP[0]}}, OP[0]};  // Bit_Extender bit_extender_1
  assign xor_1_out = B ^ bit_extender_1_out;  // XOR_Gate xor_1, 8 bits wide
  Barrel_Shifter barrel_shifter_1 (.S(B[2:0]), .D(A), .Y(barrel_shifter_1_y));
  Adder adder_1 (.a(A), .b(xor_1_out), .out(adder_1_out), .cin(OP[0]));  // open: cout
  Multiplexer #(.width(8), .enable("false")) multiplexer_1 (
    .in0(barrel_shifter_1_y), .in1(B), .out(multiplexer_1_out), .sel(OP[0]));
  Multiplexer #(.width(8), .enable("false")) multiplexer_2 (
    .in0(adder_1_out), .in1(multiplexer_1_out), .out(R), .sel(OP[1]));
  nor nor_1 (Z, R[0], R[1], R[2], R[3], R[4], R[5], R[6], R[7]);
endmodule

module Barrel_Shifter (
  input  [2:0] S,
  input  [7:0] D,
  output [7:0] Y
);

  Multiplexer #(.select(3), .enable("false")) multiplexer_1 (
    .in0(D[0]), .in1(D[1]), .in2(D[2]), .in3(D[3]), .in4(D[4]), .in5(D[5]), .in6(D[6]), .in7(D[7]),
    .out(Y[0]), .sel(S));
  Multiplexer #(.select(3), .enable("false")) multiplexer_2 (
    .in0(D[1]), .in1(D[2]), .in2(D[3]), .in3(D[4]), .in4(D[5]), .in5(D[6]), .in6(D[7]), .in7(1'b0),
    .out(Y[1]), .sel(S));
  Multiplexer #(.select(3), .enable("false")) multiplexer_3 (
    .in0(D[2]), .in1(D[3]), .in2(D[4]), .in3(D[5]), .in4(D[6]), .in5(D[7]), .in6(1'b0), .in7(1'b0),
    .out(Y[2]), .sel(S));
  Multiplexer #(.select(3), .enable("false")) multiplexer_4 (
    .in0(D[3]), .in1(D[4]), .in2(D[5]), .in3(D[6]), .in4(D[7]), .in5(1'b0), .in6(1'b0), .in7(1'b0),
    .out(Y[3]), .sel(S));
  Multiplexer #(.select(3), .enable("false")) multiplexer_5 (
    .in0(D[4]), .in1(D[5]), .in2(D[6]), .in3(D[7]), .in4(1'b0), .in5(1'b0), .in6(1'b0), .in7(1'b0),
    .out(Y[4]), .sel(S));
  Multiplexer #(.select(3), .enable("false")) multiplexer_6 (
    .in0(D[5]), .in1(D[6]), .in2(D[7]), .in3(1'b0), .in4(1'b0), .in5(1'b0), .in6(1'b0), .in7(1'b0),
    .out(Y[5]), .sel(S));
  Multiplexer #(.select(3), .enable("false")) multiplexer_7 (
    .in0(D[6]), .in1(D[7]), .in2(1'b0), .in3(1'b0), .in4(1'b0), .in5(1'b0), .in6(1'b0), .in7(1'b0),
    .out(Y[6]), .sel(S));
  Multiplexer #(.select(3), .enable("false")) multiplexer_8 (
    .in0(D[7]), .in1(1'b0), .in2(1'b0), .in3(1'b0), .in4(1'b0), .in5(1'b0), .in6(1'b0), .in7(1'b0),
    .out(Y[7]), .sel(S));
endmodule

module CPU (
);

  wire alu_1_z, CP1, CP2, d_ff_1_p4, EF, ER, Flags, MCLK_out, not_2_out, nRD, nWR, RST, SC, SE, SI, SO;
  wire [1:0] OPA, SD;
  wire [2:0] interconnections_1_aa, interconnections_1_ab, interconnections_1_ad, Opcode;
  wire [7:0] alu_1_r, controlled_buffer_1_out, Ext_output, multiplexer_3_out, multiplexer_4_out,
       Register_File_a, Register_File_b, Register_File_r0, Register_File_r0_2, Register_File_r1,
       Register_File_r1_2, Register_File_r2, Register_File_r2_2, Register_File_r3, Register_File_r3_2;
  wire [8:0] interconnections_1_imm;
  wire [9:0] adder_1_out, LExt_o, multiplexer_1_out, multiplexer_2_out, PC_q, Rext_o;
  wire [11:0] Code_memory_data;

  LExt LExt (.I(interconnections_1_imm), .O(LExt_o));
  Multiplexer #(.width(10), .disabled(0), .enable("false")) multiplexer_1 (
    .in0(LExt_o), .in1(10'h1), .out(multiplexer_1_out), .sel(SO));
  Clock MCLK (.out(MCLK_out));
  Button MRST (.out(RST));
  Instruction_Decoder instruction_decoder_1 (
    .Opcode(Opcode), .Flags(Flags), .nRD(nRD), .nWR(nWR), .EF(EF), .SC(SC), .SE(SE), .ER(ER), .OPA(OPA),
    .SI(SI), .SO(SO), .SD(SD));
  Adder #(.width(10)) adder_1 (.a(PC_q), .b(multiplexer_1_out), .out(adder_1_out));  // open: cin, cout
  RExt Rext (.I(Register_File_a), .O(Rext_o));
  Multiplexer #(.width(10), .disabled(0), .enable("false")) multiplexer_2 (
    .in0(adder_1_out), .in1(Rext_o), .out(multiplexer_2_out), .sel(SI));
  // D_Flip_Flop #(.NegatePresetClear("false")) d_ff_1: pin names not known; wires that end beside it: 1'b1, MCLK_out, RST, d_ff_1_p4
  Register #(.width(10)) PC (.D(multiplexer_2_out), .Q(PC_q), .clk(CP1), .clr(RST));  // open: en
  or or_1 (CP1, MCLK_out, d_ff_1_p4);
  not not_1 (CP2, CP1);
  Interconnections interconnections_1 (
    .Instruction(Code_memory_data), .AB(interconnections_1_ab), .AA(interconnections_1_aa),
    .AD(interconnections_1_ad), .Opcode(Opcode), .Imm(interconnections_1_imm));
  ROM #(.addrWidth(10), .dataWidth(12)) Code_memory (.addr(PC_q), .data(Code_memory_data));  // open: sel
  // Probe on Code_memory_data
  Register_File Register_File (
    .WE(ER), .Clk(CP1), .D(multiplexer_4_out), .A(Register_File_a), .B(Register_File_b),
    .R0(Register_File_r0), .R1(Register_File_r1), .R2(Register_File_r2), .R3(Register_File_r3),
    .AA(interconnections_1_aa), .AB(interconnections_1_ab), .AD(interconnections_1_ad),
    .R0_2(Register_File_r0_2), .R1_2(Register_File_r1_2), .R2_2(Register_File_r2_2), .R3_2(Register_File_r3_2));
  Ext Ext (.Input(interconnections_1_imm), .Output(Ext_output), .Sel(SE));
  // Probe on Register_File_r0
  // Probe on Register_File_r1
  // Probe on Register_File_r2
  // Probe on Register_File_r3
  // Probe on Register_File_r0_2
  // Probe on Register_File_r1_2
  // Probe on Register_File_r2_2
  // Probe on Register_File_r3_2
  // Probe on Ext_output
  // Probe on Register_File_a
  // Probe on Register_File_b
  ALU alu_1 (.A(Register_File_a), .B(multiplexer_3_out), .Z(alu_1_z), .R(alu_1_r), .OP(OPA));
  Multiplexer #(.width(8), .enable("false")) multiplexer_3 (
    .in0(Register_File_b), .in1(Ext_output), .out(multiplexer_3_out), .sel(SC));
  not not_2 (not_2_out, nWR);
  assign controlled_buffer_1_out = not_2_out ? Register_File_a : 8'bz;  // Controlled_Buffer controlled_buffer_1
  // Probe on alu_1_r
  Register #(.width(1)) CPSR (.D(alu_1_z), .en(EF), .Q(Flags), .clk(CP1), .clr(1'b0));
  RAM #(.bus("synch")) Data_memory (.addr(alu_1_r), .data(controlled_buffer_1_out));  // open: sel, clk, ld, clr
  // Probe on controlled_buffer_1_out
  Multiplexer #(.select(2), .width(8), .enable("false")) multiplexer_4 (
    .in0(controlled_buffer_1_out), .in1(alu_1_r), .in2(Ext_output), .out(multiplexer_4_out), .sel(SD));  // open: in3
  // Probe on multiplexer_4_out

  // Notes on the sheet:
  //   contents of Code_memory (hex, n*v repeats v):
  //   6 206 426 80e 601 258 20 12 85 254 57 3
endmodule

module Ext (
  input  [8:0] Input,
  input  Sel,
  output [7:0] Output
);

  wire [7:0] bit_extender_1_out, bit_extender_2_out;

  assign bit_extender_1_out = {{5{1'b0}}, Input[2:0]};  // Bit_Extender bit_extender_1
  assign bit_extender_2_out = {{2{1'b0}}, Input[5:0]};  // Bit_Extender bit_extender_2
  Multiplexer #(.width(8), .enable("false")) multiplexer_1 (
    .in0(bit_extender_1_out), .in1(bit_extender_2_out), .out(Output), .sel(Sel));
endmodule

module Instruction_Decoder (
  input  Flags,
  input  [2:0] Opcode,
  output [1:0] SD,
  output nRD,
  output nWR,
  output EF,
  output SC,
  output SE,
  output ER,
  output SI,
  output SO,
  output [1:0] OPA
);

  ROM #(.addrWidth(4), .dataWidth(10)) rom_1 (
    .addr({Opcode, Flags}), .data({SO, SI, ER, SE, SC, EF, nWR, nRD, SD}));  // open: sel

  assign OPA = Opcode[2:1];

  // Notes on the sheet:
  //   contents of rom_1 (hex, n*v repeats v):
  //   29d 29d 2a8 2a8 21d 21d 6 6 2bd 2bd 30c 20c 2ce 2ce 204 204
endmodule

module Interconnections (
  input  [11:0] Instruction,
  output [2:0] Opcode,
  output [2:0] AB,
  output [2:0] AA,
  output [2:0] AD,
  output [8:0] Imm
);


  assign AA = Instruction[8:6];
  assign AB = Instruction[5:3];
  assign AD = Instruction[11:9];
  assign Imm = Instruction[11:3];
  assign Opcode = Instruction[2:0];
endmodule

module LExt (
  input  [8:0] I,
  output [9:0] O
);

  assign O = {{1{1'b0}}, I};  // Bit_Extender bit_extender_1
endmodule

module Register_File (
  input  Clk,
  input  [7:0] D,
  input  WE,
  input  [2:0] AD,
  input  [2:0] AB,
  input  [2:0] AA,
  output [7:0] R0,
  output [7:0] R1,
  output [7:0] R2,
  output [7:0] R3,
  output [7:0] R0_2,
  output [7:0] R1_2,
  output [7:0] R2_2,
  output [7:0] R3_2,
  output [7:0] A,
  output [7:0] B
);

  wire demultiplexer_1_out0, demultiplexer_1_out1, demultiplexer_1_out2, demultiplexer_1_out3,
       demultiplexer_1_out4, demultiplexer_1_out5, demultiplexer_1_out6, demultiplexer_1_out7;

  Demultiplexer #(.select(3), .disabled(0), .enable("false")) demultiplexer_1 (
    .out0(demultiplexer_1_out0), .out1(demultiplexer_1_out1), .out2(demultiplexer_1_out2),
    .out3(demultiplexer_1_out3), .out4(demultiplexer_1_out4), .out5(demultiplexer_1_out5),
    .out6(demultiplexer_1_out6), .out7(demultiplexer_1_out7), .in(WE), .sel(AD));
  Register u_R0 (.D(D), .en(demultiplexer_1_out0), .Q(R0), .clk(Clk));  // open: clr
  Register u_R1 (.D(D), .en(demultiplexer_1_out1), .Q(R1), .clk(Clk));  // open: clr
  Register u_R2 (.D(D), .en(demultiplexer_1_out2), .Q(R2), .clk(Clk));  // open: clr
  Register u_R3 (.D(D), .en(demultiplexer_1_out3), .Q(R3), .clk(Clk));  // open: clr
  Register R4 (.D(D), .en(demultiplexer_1_out4), .Q(R0_2), .clk(Clk));  // open: clr
  Register R5 (.D(D), .en(demultiplexer_1_out5), .Q(R1_2), .clk(Clk));  // open: clr
  Register R6 (.D(D), .en(demultiplexer_1_out6), .Q(R2_2), .clk(Clk));  // open: clr
  Register R7 (.D(D), .en(demultiplexer_1_out7), .Q(R3_2), .clk(Clk));  // open: clr
  Multiplexer #(.select(3), .width(8), .disabled(0), .enable("false")) multiplexer_1 (
    .in0(R0), .in1(R1), .in2(R2), .in3(R3), .in4(R0_2), .in5(R1_2), .in6(R2_2), .in7(R3_2), .out(B), .sel(AB));
  Multiplexer #(.select(3), .width(8), .disabled(0), .enable("false")) multiplexer_2 (
    .in0(R0), .in1(R1), .in2(R2), .in3(R3), .in4(R0_2), .in5(R1_2), .in6(R2_2), .in7(R3_2), .out(A), .sel(AA));
endmodule

module RExt (
  input  [7:0] I,
  output [9:0] O
);

  assign O = {{2{1'b0}}, I};  // Bit_Extender bit_extender_1
endmodule
